// Logisim project IT012_Lab01_25520105.circ as structural Verilog: 6 circuits, main circuit Warmup
module Warmup (
  input  A,
  input  B,
  output F
);

  wire not_1_out;

  not not_1 (not_1_out, B);
  and and_1 (F, A, not_1_out);
endmodule

module tn1 (
  input  A,
  input  C,
  input  B,
  output NOTA,
  output AND,
  output OR,
  output NAND_Chain,
  output NOR,
  output XOR3,
  output XNOR,
  output NAND3
);

  wire nand_1_out;

  nand nand_1 (nand_1_out, B, A);
  not not_1 (NOTA, A);
  and and_1 (AND, A, B);
  or or_1 (OR, A, B);
  nand nand_2 (NAND_Chain, nand_1_out, C);
  nor nor_1 (NOR, A, B);
  xor xor_1 (XOR3, A, C, B);
  xnor xnor_1 (XNOR, A, B);
  nand nand_3 (NAND3, A, C, B);
endmodule

module TN2 (
  input  x,
  input  y,
  input  z,
  output EQ1,
  output EQ2,
  output EQ3,
  output EQ4,
  output EQ5
);

  wire and_1_out, and_2_out, and_3_out, and_4_out, and_5_out, and_6_out, nand_1_out, nor_1_out, not_1_out,
       not_2_out, not_3_out, not_4_out, not_5_out, not_6_out, or_1_out, or_2_out, or_3_out, or_4_out,
       or_5_out, or_6_out;

  not not_1 (not_1_out, x);
  and and_1 (and_1_out, y, z);
  not not_2 (not_2_out, x);
  and and_2 (and_2_out, not_1_out, y);
  nor nor_1 (nor_1_out, x, y);
  not not_3 (not_3_out, x);
  and and_3 (and_3_out, not_3_out, not_4_out);
  not not_4 (not_4_out, y);
  not not_5 (not_5_out, x);
  and and_4 (and_4_out, not_5_out, not_6_out);
  not not_6 (not_6_out, y);
  or or_1 (or_1_out, x, y);
  or or_2 (or_2_out, x, z);
  and and_5 (and_5_out, not_2_out, y);
  or or_3 (or_3_out, x, y);
  nand nand_1 (nand_1_out, x, y);
  or or_4 (or_4_out, x, and_1_out);
  and and_6 (and_6_out, or_1_out, or_2_out);
  or or_5 (or_5_out, x, and_5_out);
  or or_6 (or_6_out, x, and_2_out);
  xnor xnor_1 (EQ1, nor_1_out, and_3_out);
  xnor xnor_2 (EQ2, nand_1_out, and_4_out);
  xnor xnor_3 (EQ3, or_4_out, and_6_out);
  xnor xnor_4 (EQ4, x, or_5_out);
  xnor xnor_5 (EQ5, or_3_out, or_6_out);
endmodule

module TN3 (
  input  A,
  input  B,
  input  C,
  input  D,
  output F
);

  wire and_1_out, and_2_out, and_3_out, and_4_out, and_5_out, and_6_out, not_1_out, not_2_out, not_3_out,
       not_4_out;

  not not_1 (not_1_out, A);
  not not_2 (not_2_out, B);
  not not_3 (not_3_out, C);
  not not_4 (not_4_out, D);
  and and_1 (and_1_out, not_1_out, not_2_out, C, not_4_out);
  and and_2 (and_2_out, not_1_out, not_2_out, C, D);
  and and_3 (and_3_out, not_1_out, B, not_3_out, D);
  and and_4 (and_4_out, not_1_out, B, C, D);
  and and_5 (and_5_out, A, not_2_out, C, D);
  and and_6 (and_6_out, A, B, not_3_out, D);
  or or_1 (F, and_1_out, and_2_out, and_3_out, and_4_out, and_5_out, and_6_out);
endmodule

module TN4 (
  input  A,
  input  B,
  input  C,
  input  D,
  output F_can,
  output F_pos,
  output F_sop,
  output EQ2,
  output EQ1
);

  wire and_2_out, and_3_out, and_4_out, and_5_out, and_6_out, and_7_out, and_8_out, and_9_out, and_10_out,
       and_11_out, not_1_out, not_2_out, not_3_out, not_4_out, or_1_out, or_2_out, or_3_out, or_4_out;

  and and_1 (F_pos, or_1_out, or_2_out, or_3_out, or_4_out);
  or or_1 (or_1_out, B, C);
  or or_2 (or_2_out, not_2_out, D);
  or or_3 (or_3_out, not_1_out, D);
  or or_4 (or_4_out, not_1_out, not_2_out, not_3_out);
  not not_1 (not_1_out, A);
  xnor xnor_1 (EQ2, F_pos, F_can);
  not not_2 (not_2_out, B);
  not not_3 (not_3_out, C);
  not not_4 (not_4_out, D);
  xnor xnor_2 (EQ1, F_sop, F_can);
  and and_2 (and_2_out, not_1_out, not_2_out, C, not_4_out);
  and and_3 (and_3_out, not_1_out, not_2_out, C, D);
  and and_4 (and_4_out, not_1_out, B, not_3_out, D);
  and and_5 (and_5_out, not_1_out, B, C, D);
  and and_6 (and_6_out, A, not_2_out, C, D);
  and and_7 (and_7_out, A, B, not_3_out, D);
  and and_8 (and_8_out, B, not_3_out, D);
  and and_9 (and_9_out, not_1_out, C, D);
  and and_10 (and_10_out, not_2_out, C, D);
  and and_11 (and_11_out, not_1_out, not_2_out, C);
  or or_5 (F_can, and_2_out, and_3_out, and_4_out, and_5_out, and_6_out, and_7_out);
  or or_6 (F_sop, and_8_out, and_9_out, and_10_out, and_11_out);
endmodule

module TN5 (
  input  A,
  input  B,
  input  C,
  input  D,
  input  E,
  output XOR
);

  wire xor_1_out, xor_2_out, xor_3_out;

  xor xor_1 (xor_1_out, A, B);
  xor xor_2 (xor_2_out, xor_1_out, C);
  xor xor_3 (xor_3_out, xor_2_out, D);
  xor xor_4 (XOR, xor_3_out, E);
endmodule
